# Fritzing sketch Skittle Dispenser (saved by Fritzing 0.9.3b)
breadboards: 1

parts:
  Part1 = PocketBeagle
  J1 = Basic Servo
  Part2 = 0.56" 7-segment LED Backpack [part_number=879]
  R1 = Resistor [tolerance=±5% resistance=220 package=THT]
  R2 = Resistor [tolerance=±5% resistance=220 package=THT]
  J2 = Piezo Speaker
  R3 = Resistor [tolerance=±5% resistance=220 package=THT]
  J3 = Basic Force Sensing Resistor (FSR) [package=THT]
  R4 = Resistor [tolerance=±5% resistance=220 package=THT]

nets:
  N1: Part1.3.3V, R1.Pin_1, R2.Pin_1, R3.Pin_0, J3.pin_1
  GND: Part1.GND, J1.gnd, Part2.GND, J2.pin1, R4.Pin_0
  VCC: Part1.VOUT, J1.vcc, Part2.VDD
  N2: Part1.PWM1A, J1.pulse
  N3: Part1.GPIO59, R3.Pin_1
  N4: Part1.GPIO23, J2.pin2
  N5: Part1.I2C1.SCL, Part2.SCL, R1.Pin_0
  N6: Part1.I2C1.SDA, Part2.SDA, R2.Pin_0
  N7: Part1.AIN5/GPIO86, J3.pin_0, R4.Pin_1

notes:
  Wires go to power and ground on IR breakbeam transmitter.
  Wires go to power, ground, and signal on IR breakbeam receiver.
  NOTE: There is no IR sensor part in Fritzing. Therefore, the IR sensor connections will be designated with notes.

custom parts:
  0.56" 7-segment LED Backpack: This 0.56" 7-segment LED display includes a driver chip for simple control via an I2C interface. The backpack features address-selection jumpers so you can connect up to eight displays on a single I2C bus.
